# Fritzing sketch smart_coffee (saved by Fritzing 0.9.3b)
breadboards: 1

parts:
  U1 = NodeMCU V1.0
  Current_Sensor1 = ACS-715

nets:
  N1: U1.D1, U1.3V3
  GND: U1.GND, Current_Sensor1.GND
  VIN: U1.Vin, Current_Sensor1.Vcc
  N2: U1.A0, Current_Sensor1.VIOUT

notes:
  Fio Cinza: Modo Smart Config (Mudar D1 - GND em 3 segundos para D1 - 3.3 V)

custom parts:
  NodeMCU V1.0: ESP8266 based NodeMCU
  ACS-715: Breakout Board with ACS 714/715 Hall Effect-Based Linear Current Sensor from Pololu This board is a simple carrier for Allegro’s 30A ACS 714/715 Hall effect-based linear current sensor. This version accepts a unidirectional current input up to 30 A. The output is an analog voltage (133 mV/A) that reads 500 mV for no input current and has a typical error of less than 1.5%.
